# Fritzing sketch schema (saved by Fritzing 0.9.9b)
breadboards: 1

parts:
  Part1 = Arduino Uno (Rev3) - ICSP
  Q2 = TIP120 Hi-Current Darlington Transistor
  KY-1 = Keyes Hall Effect Sensor [package=THT]
  D1 = Zener Diode [part_number=1N4732A breakdown_voltage=3.6V package="300 mil [THT]"]
  R1 = Resistor [tolerance=±5% resistance=1000 package="0805 [SMD]"]

nets:
  N1: Part1.D13/SCK, R1.Pin_0
  N2: Part1.D7, KY-1.signal
  N3: Part1.5V, KY-1.power
  N4: Part1.GND, Q2.EMITTER, KY-1.ground
  N5: Part1.VIN, D1.cathode
  N6: Q2.BASE, R1.Pin_1
  N7: Q2.COLLECTOR, D1.anode

notes:
  Solenoïd

custom parts:
  Keyes Hall Effect Sensor: Keyes Magnetic Hall Effect Sensor Module for Arduino. Working voltage: 4.5V-25V.
